# Fritzing sketch Nightlight (saved by Fritzing 0.9.10b)
perfboards: 1

parts:
  LED1 = RGB LED - (4 legs) [package="5 mm [THT]"]  # not connected
  R1 = PHOTOCELL [package=photocell-kit]  # not connected
  R2 = Resistor [tolerance=±5% resistance=10k package="0805 [SMD]"]  # not connected
  R3 = Resistor [tolerance=±5% resistance=220 package="0805 [SMD]"]
  R4 = Resistor [tolerance=±5% resistance=220 package="0805 [SMD]"]
  IR1 = TSOP312.., 314.. [package=THT]
  R5 = Resistor [tolerance=±5% power=0.25 resistance=220 package=THT]
  Part1 = Arduino Uno (Rev3) - ICSP
  Part2 = HC-SR501 Body Sensor Module
  Grove1 = Grove OLED 128x96
  Mod1 = KY-015 Temperature & Humidity Sensor Module [package="Breakout board"]

nets:
  N1: R3.Pin_1, Part1.D5_PWM
  N2: R4.Pin_1, Part1.D6_PWM
  N3: IR1.Data, Part1.D11_PWM/MOSI
  N4: R5.Pin_1, Part1.D3_PWM
  N5: Part1.D10_PWM/SS, Mod1.S
  N6: Part1.A4/SDA, Grove1.SCL
  N7: Part1.A5/SCL, Grove1.SDA
  N8: Part1.D7, Part2.GND

custom parts:
  HC-SR501 Body Sensor Module: Pyroelectric Infrared PIR Motion Sensor Detector Module
  KY-015 Temperature & Humidity Sensor Module: KY-015 temperature and humidity sensor module, provides a low-latency serial interface to measure humidity and temperature.
